// Logisim project cpu.circ as structural Verilog: 5 circuits, main circuit main
module main (
  input  RESET,
  input  [31:0] in_2,
  input  [31:0] in_3
);

  wire CLK, control_unit_1_ir_write, control_unit_1_pc_write, control_unit_1_ram_oe;
  wire [1:0] control_unit_1_pc_cmd, control_unit_1_pc_isize;
  wire [15:0] bit_extender_1_out;
  wire [31:0] adder_1_out, INSTRUCTION_REG_stored, PROGRAM_COUNTER_address, ram_1_data;

  Clock clock_1 (.out(CLK));
  Adder #(.width(32)) adder_1 (.a(in_2), .b(PROGRAM_COUNTER_address), .out(adder_1_out), .cin(1'b0));  // open: cout
  COUNTER32b PROGRAM_COUNTER (
    .JUMP_ADDRESS(in_3), .INSTRUCTION_SIZE(control_unit_1_pc_isize), .CMD(control_unit_1_pc_cmd),
    .WRITE(control_unit_1_pc_write), .CLOCK(CLK), .RESET(RESET), .ADDRESS(PROGRAM_COUNTER_address));
  RAM #(.addrWidth(16), .asyncread("true"), .dataWidth(32), .databus("bidir")) ram_1 (
    .addr(bit_extender_1_out), .oe(control_unit_1_ram_oe), .clk(CLK), .data(ram_1_data));  // open: we
  Bit_Extender #(.in_width(32), .\type ("zero")) bit_extender_1 (.in(adder_1_out), .out(bit_extender_1_out));
  REGISTER32b INSTRUCTION_REG (
    .DATA(ram_1_data), .WRITE(control_unit_1_ir_write), .CLOCK(CLK), .RESET(RESET),
    .STORED(INSTRUCTION_REG_stored));
  CONTROL_UNIT control_unit_1 (
    .INSTRUCTION(INSTRUCTION_REG_stored), .CLOCK(CLK), .RESET(RESET), .IR_WRITE(control_unit_1_ir_write),
    .RAM_OE(control_unit_1_ram_oe), .PC_ISIZE(control_unit_1_pc_isize), .PC_CMD(control_unit_1_pc_cmd),
    .PC_WRITE(control_unit_1_pc_write));
endmodule

module RAM_CONTROLLER (
  input  [31:0] WRITEIN,
  input  [20:0] ADDRESS,
  input  WRITESTART,
  input  READSTART,
  input  CLK,
  output [31:0] READOUT
);

  wire and_1_out, and_2_out, and_3_out, d_ff_1_q, d_ff_2_q, d_ff_5_q, demultiplexer_1_out0,
       demultiplexer_1_out1, demultiplexer_2_out0, demultiplexer_2_out1, demultiplexer_2_out2,
       demultiplexer_2_out3, multiplexer_1_out, not_1_out, not_2_out, or_1_out, s_r_ff_1_q, xor_1_out,
       xor_2_out, xor_3_out;
  wire [1:0] d_ff_3_q;
  wire [7:0] multiplexer_2_out, RAM1_data;
  wire [20:0] adder_1_out;

  D_Flip_Flop d_ff_1 (.D(WRITESTART), .clk(CLK), .Q(d_ff_1_q));  // open: Qn, preset, reset
  D_Flip_Flop d_ff_2 (.D(READSTART), .clk(CLK), .Q(d_ff_2_q));  // open: Qn, preset, reset
  and and_1 (and_1_out, WRITESTART, not_1_out);
  not not_1 (not_1_out, d_ff_1_q);
  and and_2 (and_2_out, READSTART, not_2_out);
  not not_2 (not_2_out, d_ff_2_q);
  or or_1 (or_1_out, and_1_out, and_2_out);
  Multiplexer multiplexer_1 (.in0(d_ff_5_q), .in1(and_2_out), .out(multiplexer_1_out), .sel(or_1_out));
  D_Flip_Flop d_ff_3 (.D(xor_1_out), .clk(CLK), .Q(d_ff_3_q[0]), .reset(xor_3_out));  // open: Qn, preset
  xor xor_1 (xor_1_out, d_ff_3_q[0], 1'b1);
  D_Flip_Flop d_ff_4 (.D(xor_2_out), .clk(CLK), .Q(d_ff_3_q[1]), .reset(xor_3_out));  // open: Qn, preset
  xor xor_2 (xor_2_out, d_ff_3_q[1], d_ff_3_q[0]);
  Adder #(.width(21)) adder_1 (.a({{19{1'b0}}, d_ff_3_q}), .b(ADDRESS), .out(adder_1_out), .cin(1'b0));  // open: cout
  S_R_Flip_Flop s_r_ff_1 (.S(or_1_out), .R(and_3_out), .clk(CLK), .Q(s_r_ff_1_q));  // open: reset, Qn, preset
  D_Flip_Flop d_ff_5 (.D(multiplexer_1_out), .clk(CLK), .Q(d_ff_5_q));  // open: Qn, preset, reset
  xor xor_3 (xor_3_out, 1'b1, s_r_ff_1_q);
  and and_3 (and_3_out, d_ff_3_q[0], d_ff_3_q[1]);
  Demultiplexer demultiplexer_1 (
    .out0(demultiplexer_1_out0), .out1(demultiplexer_1_out1), .in(s_r_ff_1_q), .sel(d_ff_5_q));
  RAM #(.addrWidth(21), .asyncread("true"), .databus("bidir")) RAM1 (
    .addr(adder_1_out), .we(demultiplexer_1_out0), .oe(demultiplexer_1_out1), .clk(CLK), .data(RAM1_data));
  Multiplexer #(.select(2), .width(8)) multiplexer_2 (
    .in0(WRITEIN[31:24]), .in1(WRITEIN[23:16]), .in2(WRITEIN[15:8]), .in3(WRITEIN[7:0]),
    .out(multiplexer_2_out), .sel(d_ff_3_q));
  assign RAM1_data = demultiplexer_1_out0 ? multiplexer_2_out : 8'bz;  // Controlled_Buffer controlled_buffer_1
  Demultiplexer #(.select(2)) demultiplexer_2 (
    .out0(demultiplexer_2_out0), .out1(demultiplexer_2_out1), .out2(demultiplexer_2_out2),
    .out3(demultiplexer_2_out3), .in(demultiplexer_1_out1), .sel(d_ff_3_q));
  Register register_1 (.D(RAM1_data), .en(demultiplexer_2_out0), .clk(CLK), .Q(READOUT[31:24]));  // open: clr
  Register register_2 (.D(RAM1_data), .en(demultiplexer_2_out1), .clk(CLK), .Q(READOUT[23:16]));  // open: clr
  Register register_3 (.D(RAM1_data), .en(demultiplexer_2_out2), .clk(CLK), .Q(READOUT[15:8]));  // open: clr
  Register register_4 (.D(RAM1_data), .en(demultiplexer_2_out3), .clk(CLK), .Q(READOUT[7:0]));  // open: clr
endmodule

module REGISTER32b (
  input  [31:0] DATA,
  input  WRITE,
  input  CLOCK,
  input  RESET,
  output [31:0] STORED
);

  Register #(.width(32)) register_1 (.D(DATA), .en(WRITE), .clk(CLOCK), .Q(STORED), .clr(RESET));
  Hex_Digit_Display hex_digit_display_1 (.value(STORED[31:28]));  // open: dp
  Hex_Digit_Display hex_digit_display_2 (.value(STORED[27:24]));  // open: dp
  Hex_Digit_Display hex_digit_display_3 (.value(STORED[23:20]));  // open: dp
  Hex_Digit_Display hex_digit_display_4 (.value(STORED[19:16]));  // open: dp
  Hex_Digit_Display hex_digit_display_5 (.value(STORED[15:12]));  // open: dp
  Hex_Digit_Display hex_digit_display_6 (.value(STORED[11:8]));  // open: dp
  Hex_Digit_Display hex_digit_display_7 (.value(STORED[7:4]));  // open: dp
  Hex_Digit_Display hex_digit_display_8 (.value(STORED[3:0]));  // open: dp
endmodule

module COUNTER32b (
  input  [31:0] JUMP_ADDRESS,
  input  [1:0] INSTRUCTION_SIZE,
  input  CLOCK,
  input  RESET,
  input  [1:0] CMD,
  input  WRITE,
  output [31:0] ADDRESS
);

  wire [31:0] adder_1_out, bit_extender_1_out, multiplexer_1_out;

  Adder #(.width(32)) adder_1 (.a(ADDRESS), .b(bit_extender_1_out), .out(adder_1_out), .cin(1'b0));  // open: cout
  assign bit_extender_1_out = {{30{1'b0}}, INSTRUCTION_SIZE};  // Bit_Extender bit_extender_1
  Multiplexer #(.select(2), .width(32)) multiplexer_1 (
    .in0(ADDRESS), .in1(adder_1_out), .in2(JUMP_ADDRESS), .in3({32{1'b0}}), .out(multiplexer_1_out), .sel(CMD));
  REGISTER32b register32b_1 (.DATA(multiplexer_1_out), .WRITE(WRITE), .CLOCK(CLOCK), .RESET(RESET), .STORED(ADDRESS));
endmodule

module CONTROL_UNIT (
  input  [31:0] INSTRUCTION,
  input  CLOCK,
  input  RESET,
  output IR_WRITE,
  output RAM_OE,
  output [1:0] PC_ISIZE,
  output [1:0] PC_CMD,
  output PC_WRITE
);

  wire [1:0] controlled_buffer_1_out, controlled_buffer_2_out;

  D_Flip_Flop FETCH (.D(PC_WRITE), .clk(CLOCK), .Q(IR_WRITE), .preset(RESET), .reset(1'b0));  // open: Qn
  assign controlled_buffer_1_out = IR_WRITE ? 2'b01 : 2'bz;  // Controlled_Buffer controlled_buffer_1
  assign controlled_buffer_2_out = IR_WRITE ? 2'b01 : 2'bz;  // Controlled_Buffer controlled_buffer_2
  Register #(.width(2)) register_1 (.D(controlled_buffer_1_out), .en(IR_WRITE), .clk(CLOCK), .Q(PC_ISIZE), .clr(RESET));
  Register #(.width(2)) register_2 (.D(controlled_buffer_2_out), .en(IR_WRITE), .clk(CLOCK), .Q(PC_CMD), .clr(RESET));
  D_Flip_Flop STEP (.D(IR_WRITE), .clk(CLOCK), .Q(PC_WRITE), .preset(1'b0), .reset(RESET));  // open: Qn

  assign RAM_OE = IR_WRITE;

  // Other names for the same wires on the sheet: CLK = CLOCK; FETCH = IR_WRITE; STEP = PC_WRITE
endmodule
